# Fritzing sketch Examen Final Simulador (saved by Fritzing 0.9.10b)
breadboards: 1

parts:
  Part1 = Soil Moisture Sensor
  Part2 = Arduino Uno (Rev3) - ICSP
  WeMos_D1_Mini_Relay_Shield1 = WeMos D1 Mini Relay Shield  # not connected
  Part3 = Bluetooth HC-05 Macho
  LCD1 = LCD screen
  VCC1 = Battery  # not connected
  R1 = Trimmer Potentiometer [maximum_resistance=10kΩ knob_status=50% power=0.5W package=THT]
  M1 = DC Motor [voltage_(max)=6V voltage_(min)=3V]  # not connected
  R2 = Resistor [tolerance=±5% resistance=220 package="2512 [SMD]"]
  S1 = Pushbutton [package="[THT]"]
  R3 = Resistor [tolerance=±5% resistance=220 package="2512 [SMD]"]

nets:
  N1: Part1.SIG, Part2.A0
  GND: Part1.GND, Part3.GND, LCD1.VSS, LCD1.R/W, LCD1.LED-, R1.leg2, S1.Pin_3, S1.Pin_4
  VCC: Part1.VCC, Part3.VCC, LCD1.VDD, R1.leg1, R2.Pin_0, R3.Pin_1
  N2: Part2.D10_PWM/SS, S1.Pin_1, S1.Pin_2, R3.Pin_0
  N3: Part2.D12/MISO, Part3.TXD
  N4: Part2.D13/SCK, Part3.RXD
  N5: Part2.D2, LCD1.DB7
  N6: Part2.D3_PWM, LCD1.DB6
  N7: Part2.D4, LCD1.DB5
  N8: Part2.D5_PWM, LCD1.DB4
  N9: Part2.D6_PWM, LCD1.E
  N10: Part2.D7, LCD1.RS
  N11: LCD1.V0, R1.wiper
  N12: LCD1.LED+, R2.Pin_1
